# Fritzing sketch Arduino_Shield_At328p_Programmer (saved by Fritzing 0.9.3b)
circuit board: 6.88566cm x 5.36311cm
breadboards: 1

parts:
  U1 = atmega328 [package=dip]
  XTAL1 = Crystal [frequency="16 Mhz" package=THT]
  C1 = Tantalum Capacitor [capacitance=1μF package="100 mil [THT, tantalum]"]
  C2 = Tantalum Capacitor [capacitance=1μF package="100 mil [THT, tantalum]"]
  S1 = Pushbutton [package=THT]
  R1 = Resistor [tolerance=±20% resistance=10k package=THT]
  U2 = atmega328 [package=dip]  # not connected
  PCB1 = Arduino Shield PCB  # not connected
  Part1 = Arduino Uno (Rev3)

nets:
  N1: U1.RESET, S1.leg1, R1.Pin_1, Part1.D10_PWM/SS
  VCC: U1.VCC, U1.AVCC, U1.AREF, R1.Pin_0, Part1.5V
  GND: U1.GND, C1.-, C2.-, S1.leg0, Part1.GND
  N2: U1.XLAT1, XTAL1.pin_0, C1.+
  N3: U1.XLAT2, XTAL1.pin_1, C2.+
  N4: U1.D11_(PWM), Part1.D11_PWM/MOSI
  N5: U1.D12, Part1.D12/MISO
  N6: U1.D13, Part1.D13/SCK

custom parts:
  Arduino Shield PCB: Plain PCB Shaped to fit an Arduino "Shield"
